# Fritzing sketch curcuit_diagram (saved by Fritzing 0.9.5d)
breadboards: 1

parts:
  부품1 = Arduino Uno (Rev3)
  ESP32_-_Back1 = ESP32 - CAM
  U1 = LCD-16X2 [package=lcd-16x2_noholes]  # not connected
  S1 = Pushbutton [package="[THT]"]
  S2 = Pushbutton [package="[THT]"]

nets:
  N1: 부품1.D0/RX, ESP32_-_Back1.GPIO3_/_RX
  N2: 부품1.D1/TX, ESP32_-_Back1.GPIO1_/_TX
  N3: 부품1.D2, S2.Pin_3, S2.Pin_4
  N4: 부품1.D3_PWM, S1.Pin_1, S1.Pin_2
  N5: 부품1.RESET, 부품1.GND, ESP32_-_Back1.GND#7
  5V: 부품1.5V, ESP32_-_Back1.5V
  N6: ESP32_-_Back1.GPIO0, ESP32_-_Back1.GND#12
  N7: S1.Pin_3, S1.Pin_4, S2.Pin_1, S2.Pin_2

custom parts:
  ESP32 - CAM: The ESP32-CAM has a very competitive small-size camera module that can operate independently as a minimum system with a footprint of only 27*40.5*4.5mm and a deep sleep current of up to 6mA.
